// Logisim project cpu_control_section.circ as structural Verilog: 6 circuits, main circuit CPU_MEM_1
module CPU_MEM_1 (
  input  in_1,
  input  in_2,
  output out_3
);

  wire nand_1_out, nand_2_out, nand_4_out;

  nand nand_1 (nand_1_out, in_1, in_2);
  nand nand_2 (nand_2_out, nand_1_out, in_2);
  nand nand_3 (out_3, nand_1_out, nand_4_out);
  nand nand_4 (nand_4_out, out_3, nand_2_out);

  // Notes on the sheet:
  //   in_1: pull=down
  //   in_2: pull=down
endmodule

module CPU_CONTROL_SECTION (
  input  clks,
  input  RESET,
  input  clk,
  input  clke,
  input  LOAD,
  input  MAR_S,
  input  C,
  input  A,
  input  E,
  input  Z,
  input  [7:0] IR_IN,
  output IR_S,
  output BUS_1,
  output MAR_S_2,
  output IAR_S,
  output IAR_E,
  output ACC_S,
  output RAM_E,
  output RAM_S,
  output ACC_E,
  output TMP_S,
  output IO_CLK_E,
  output FLAGS_S,
  output IO_CLKS_S,
  output R0_S,
  output R0_E,
  output R1_S,
  output R1_E,
  output R2_E,
  output R2_S,
  output R3_E,
  output out_32,
  output R3_S,
  output ALU_0,
  output ALU_1,
  output ALU_2,
  output END,
  output C_2,
  output I_O,
  output D_A
);

  wire _1, _2, _3, _4, _5, _6, ACC_E_5_IF_JUMP, ACC_E_6_ALU, ACC_E_6_DATA, ACC_S_4_DATA, ACC_S_4_IF_JUMP,
       ACC_S_5_ALU, and_5_out, and_6_out, and_7_out, and_8_out, and_9_out, and_10_out, and_11_out,
       and_12_out, and_17_out, and_19_out, and_20_out, and_21_out, and_22_out, and_23_out, and_24_out,
       and_25_out, and_26_out, and_28_out, and_35_out, and_38_out, and_39_out, and_40_out, and_52_out,
       and_53_out, and_54_out, and_55_out, and_56_out, and_57_out, and_58_out, and_60_out, and_61_out,
       and_62_out, and_63_out, and_64_out, BUS1_E_4_CL_FLAGS, cpu_decoder_2x4_1__0, cpu_decoder_2x4_1__1,
       cpu_decoder_2x4_1__2, cpu_decoder_2x4_1__3, cpu_decoder_2x4_west_1__0, cpu_decoder_2x4_west_1__1,
       cpu_decoder_2x4_west_1__2, cpu_decoder_2x4_west_1__3, cpu_decoder_2x4_west_2__0,
       cpu_decoder_2x4_west_2__1, cpu_decoder_2x4_west_2__2, cpu_decoder_2x4_west_2__3,
       cpu_decoder_3x8_cntrl_1__0, cpu_decoder_3x8_cntrl_1__1, cpu_decoder_3x8_cntrl_1__2,
       cpu_decoder_3x8_cntrl_1__3, cpu_decoder_3x8_cntrl_1__4, cpu_decoder_3x8_cntrl_1__5,
       cpu_decoder_3x8_cntrl_1__6, cpu_decoder_3x8_cntrl_1__7, cpu_stepper_1_step_1, cpu_stepper_1_step_7,
       IAR_E_4_JUMP, IAR_S_4_RE_JUMP, IAR_S_5_JUMP, IAR_S_6_IF_JUMP, MAR_S_4_LOAD, MAR_S_4_STORE, not_1_out,
       not_2_out, not_3_out, not_4_out, not_5_out, not_6_out, or_6_out, or_7_out, or_8_out, or_9_out,
       or_10_out, or_12_out, or_13_out, or_14_out, or_15_out, RAM_E_5_DATA, RAM_E_5_LOAD, RAM_S_5_STORE,
       REGB_E_4_ALU, REGB_E_4_I_O_OUTPUT, REGB_S_4_I_O_INPUT;

  or or_1 (BUS_1, _1, BUS1_E_4_CL_FLAGS, ACC_S_4_IF_JUMP, ACC_S_4_DATA);
  or or_2 (R0_E, and_5_out, and_9_out);
  or or_3 (R1_E, and_6_out, and_10_out);
  or or_4 (R2_E, and_7_out, and_11_out);
  or or_5 (R3_E, and_8_out, and_12_out);
  and and_1 (IAR_E, clke, or_6_out);
  and and_2 (RAM_E, clke, or_7_out);
  and and_3 (ACC_E, clke, or_10_out);
  and and_4 (IO_CLK_E, clke, REGB_E_4_I_O_OUTPUT);
  and and_5 (and_5_out, clke, or_8_out, cpu_decoder_2x4_west_1__0);
  and and_6 (and_6_out, clke, or_8_out, cpu_decoder_2x4_west_1__1);
  and and_7 (and_7_out, clke, or_8_out, cpu_decoder_2x4_west_1__2);
  and and_8 (and_8_out, clke, or_8_out, cpu_decoder_2x4_west_1__3);
  and and_9 (and_9_out, clke, or_9_out, cpu_decoder_2x4_west_2__0);
  and and_10 (and_10_out, clke, or_9_out, cpu_decoder_2x4_west_2__1);
  and and_11 (and_11_out, clke, or_9_out, cpu_decoder_2x4_west_2__2);
  and and_12 (and_12_out, clke, or_9_out, cpu_decoder_2x4_west_2__3);
  and and_13 (C_2, IR_IN[7], _5);
  or or_6 (or_6_out, ACC_S_4_DATA, ACC_S_4_IF_JUMP, IAR_E_4_JUMP, _1);
  or or_7 (or_7_out, RAM_E_5_LOAD, IAR_S_5_JUMP, RAM_E_5_DATA, _2, IAR_S_6_IF_JUMP);
  or or_8 (or_8_out, REGB_E_4_I_O_OUTPUT, REGB_E_4_ALU, IAR_S_4_RE_JUMP, RAM_S_5_STORE);
  or or_9 (or_9_out, ACC_S_5_ALU, MAR_S_4_STORE, MAR_S_4_LOAD);
  or or_10 (or_10_out, _3, ACC_E_6_DATA, ACC_E_6_ALU, ACC_E_5_IF_JUMP);
  and and_14 (ALU_0, _5, IR_IN[7], IR_IN[4]);
  and and_15 (ALU_1, _5, IR_IN[7], IR_IN[5]);
  and and_16 (ALU_2, _5, IR_IN[7], IR_IN[6]);
  and and_17 (and_17_out, clk, not_1_out);
  not not_1 (not_1_out, LOAD);
  and and_18 (_1, not_1_out, cpu_stepper_1_step_1);
  CPU_DECODER_2x4_WEST cpu_decoder_2x4_west_1 (
    .a(IR_IN[0]), .b(IR_IN[1]), ._0(cpu_decoder_2x4_west_1__0), ._1(cpu_decoder_2x4_west_1__1),
    ._2(cpu_decoder_2x4_west_1__2), ._3(cpu_decoder_2x4_west_1__3));
  CPU_DECODER_2x4_WEST cpu_decoder_2x4_west_2 (
    .a(IR_IN[2]), .b(IR_IN[3]), ._0(cpu_decoder_2x4_west_2__0), ._1(cpu_decoder_2x4_west_2__1),
    ._2(cpu_decoder_2x4_west_2__2), ._3(cpu_decoder_2x4_west_2__3));
  not not_2 (not_2_out, IR_IN[7]);
  CPU_STEPPER cpu_stepper_1 (
    .step_1(cpu_stepper_1_step_1), .step_2(_2), .step_3(_3), .step_4(_4), .step_5(_5), .step_6(_6),
    .step_7(cpu_stepper_1_step_7), .reset(cpu_stepper_1_step_7), .clk(and_17_out));
  CPU_DECODER_3X8_CNTRL cpu_decoder_3x8_cntrl_1 (
    .a(IR_IN[6]), .b(IR_IN[5]), .c(IR_IN[4]), ._0(cpu_decoder_3x8_cntrl_1__0),
    ._1(cpu_decoder_3x8_cntrl_1__1), ._2(cpu_decoder_3x8_cntrl_1__2), ._3(cpu_decoder_3x8_cntrl_1__3),
    ._4(cpu_decoder_3x8_cntrl_1__4), ._5(cpu_decoder_3x8_cntrl_1__5), ._6(cpu_decoder_3x8_cntrl_1__6),
    ._7(cpu_decoder_3x8_cntrl_1__7));
  and and_19 (and_19_out, not_2_out, cpu_decoder_3x8_cntrl_1__0);
  and and_20 (and_20_out, not_2_out, cpu_decoder_3x8_cntrl_1__1);
  and and_21 (and_21_out, not_2_out, cpu_decoder_3x8_cntrl_1__2);
  and and_22 (and_22_out, not_2_out, cpu_decoder_3x8_cntrl_1__3);
  and and_23 (and_23_out, not_2_out, cpu_decoder_3x8_cntrl_1__4);
  and and_24 (and_24_out, not_2_out, cpu_decoder_3x8_cntrl_1__5);
  and and_25 (and_25_out, not_2_out, cpu_decoder_3x8_cntrl_1__6);
  and and_26 (and_26_out, not_2_out, cpu_decoder_3x8_cntrl_1__7);
  and and_27 (REGB_E_4_ALU, _4, IR_IN[7]);
  and and_28 (and_28_out, IR_IN[6], IR_IN[5], IR_IN[4]);
  not not_3 (not_3_out, IR_IN[5]);
  not not_4 (not_4_out, IR_IN[4]);
  and and_29 (MAR_S_4_LOAD, _4, and_19_out);
  and and_30 (RAM_E_5_LOAD, _5, and_19_out);
  and and_31 (MAR_S_4_STORE, _4, and_20_out);
  and and_32 (RAM_S_5_STORE, _5, and_20_out);
  not not_5 (not_5_out, and_28_out);
  and and_33 (END, _4, IR_IN[7], IR_IN[6], not_3_out, not_4_out, IR_IN[3], IR_IN[2], IR_IN[1], IR_IN[0]);
  and and_34 (ACC_S_5_ALU, _5, IR_IN[7]);
  and and_35 (and_35_out, IR_IN[3], C);
  and and_36 (ACC_S_4_DATA, _4, and_21_out);
  and and_37 (ACC_S_4_IF_JUMP, and_24_out, _4);
  or or_11 (out_32, and_35_out, and_38_out, and_40_out, and_39_out);
  and and_38 (and_38_out, IR_IN[2], A);
  and and_39 (and_39_out, IR_IN[0], Z);
  and and_40 (and_40_out, IR_IN[1], E);
  and and_41 (RAM_E_5_DATA, _5, and_21_out);
  and and_42 (IAR_S_4_RE_JUMP, and_22_out, _4);
  and and_43 (ACC_E_5_IF_JUMP, and_24_out, _5);
  and and_44 (IAR_S_6_IF_JUMP, and_24_out, out_32, _6);
  and and_45 (BUS1_E_4_CL_FLAGS, _4, and_25_out);
  and and_46 (ACC_E_6_ALU, _6, IR_IN[7], not_5_out);
  CPU_DECODER_2X4 cpu_decoder_2x4_1 (
    .a(IR_IN[0]), .b(IR_IN[1]), ._0(cpu_decoder_2x4_1__0), ._1(cpu_decoder_2x4_1__1),
    ._2(cpu_decoder_2x4_1__2), ._3(cpu_decoder_2x4_1__3));
  or or_12 (or_12_out, ACC_E_6_DATA, IAR_S_5_JUMP, IAR_S_6_IF_JUMP, ACC_E_5_IF_JUMP, IAR_S_4_RE_JUMP, _3);
  and and_47 (ACC_E_6_DATA, _6, and_21_out);
  and and_48 (REGB_E_4_I_O_OUTPUT, and_26_out, _4, IR_IN[3]);
  and and_49 (IAR_E_4_JUMP, _4, and_23_out);
  and and_50 (IAR_S_5_JUMP, _5, and_23_out);
  not not_6 (not_6_out, IR_IN[3]);
  and and_51 (REGB_S_4_I_O_INPUT, and_26_out, _4, not_6_out);
  or or_13 (or_13_out, ACC_E_6_ALU, RAM_E_5_LOAD, RAM_E_5_DATA, REGB_S_4_I_O_INPUT);
  or or_14 (or_14_out, _1, ACC_S_4_DATA, ACC_S_4_IF_JUMP, IAR_E_4_JUMP, MAR_S_4_LOAD, MAR_S_4_STORE);
  or or_15 (or_15_out, ACC_S_5_ALU, ACC_S_4_IF_JUMP, ACC_S_4_DATA, _1);
  and and_52 (and_52_out, clks, _2);
  and and_53 (and_53_out, clks, or_14_out);
  and and_54 (and_54_out, clks, or_12_out);
  and and_55 (and_55_out, clks, or_15_out);
  and and_56 (and_56_out, clks, RAM_S_5_STORE);
  and and_57 (and_57_out, clks, REGB_E_4_ALU);
  and and_58 (and_58_out, clks, BUS1_E_4_CL_FLAGS);
  and and_59 (IO_CLKS_S, clks, REGB_S_4_I_O_INPUT);
  and and_60 (and_60_out, clks, or_13_out, cpu_decoder_2x4_1__0);
  and and_61 (and_61_out, clks, or_13_out, cpu_decoder_2x4_1__1);
  and and_62 (and_62_out, clks, or_13_out, cpu_decoder_2x4_1__2);
  and and_63 (and_63_out, clks, or_13_out, cpu_decoder_2x4_1__3);
  or or_16 (IR_S, RESET, and_52_out);
  or or_17 (MAR_S_2, MAR_S, and_53_out);
  or or_18 (IAR_S, RESET, and_54_out);
  or or_19 (ACC_S, RESET, and_55_out);
  and and_64 (and_64_out, clks, LOAD);
  or or_20 (TMP_S, RESET, and_57_out);
  or or_21 (FLAGS_S, RESET, and_58_out);
  or or_22 (R0_S, RESET, and_60_out);
  or or_23 (R1_S, RESET, and_61_out);
  or or_24 (R2_S, RESET, and_62_out);
  or or_25 (R3_S, RESET, and_63_out);
  or or_26 (RAM_S, and_64_out, and_56_out);

  assign D_A = IR_IN[2];
  assign I_O = IR_IN[3];

  // Other names for the same wires on the sheet: CARRY_FLAG = out_32; FLAGS_S_4_CL_FLAGS = BUS1_E_4_CL_FLAGS;
  //   ACC_E_3 = _3; IAR_S_3 = _3; IAR_S_5_IF_JUMP = ACC_E_5_IF_JUMP; IAR_S_6_DATA = ACC_E_6_DATA; INS_4 = IR_IN[3];
  //   ACC_S_1 = _1; IAR_E_1 = _1; MAR_S_1 = _1; BUS1_E_4_DATA = ACC_S_4_DATA; IAR_E_4_DATA = ACC_S_4_DATA;
  //   MAR_S_4_DATA = ACC_S_4_DATA; BUS1_E_4_IF_JUMP = ACC_S_4_IF_JUMP; IAR_E_4_IF_JUMP = ACC_S_4_IF_JUMP;
  //   MAR_S_4_IF_JUMP = ACC_S_4_IF_JUMP; MAR_S_4_JUMP = IAR_E_4_JUMP; IR_S_2 = _2; RAM_E_2 = _2;
  //   RAM_E_5_JUMP = IAR_S_5_JUMP; RAM_E_6_IF_JUMP = IAR_S_6_IF_JUMP; REGA_E_4_LOAD = MAR_S_4_LOAD;
  //   REGA_E_4_STORE = MAR_S_4_STORE; REGA_E_5_ALU = ACC_S_5_ALU; REGB_E_4_RE_JUMP = IAR_S_4_RE_JUMP;
  //   REGB_E_5_STORE = RAM_S_5_STORE; REGB_S_5_DATA = RAM_E_5_DATA; REGB_S_5_LOAD = RAM_E_5_LOAD;
  //   REGB_S_6_ALU = ACC_E_6_ALU; TMP_S_4_ALU = REGB_E_4_ALU

  // Notes on the sheet:
  //   ALL ENABLES
  //   REG B_E
  //   REG A
  //   REG B
  //   REG A
  //   REG B_S
  //   ALL SETS
endmodule

module CPU_DECODER_3X8_CNTRL (
  input  a,
  input  b,
  input  c,
  output _0,
  output _1,
  output _2,
  output _3,
  output _4,
  output _5,
  output _6,
  output _7
);

  wire not_1_out, not_2_out, not_3_out;

  not not_1 (not_1_out, c);
  not not_2 (not_2_out, b);
  not not_3 (not_3_out, a);
  and and_1 (_0, not_3_out, not_2_out, not_1_out);
  and and_2 (_1, not_3_out, not_2_out, c);
  and and_3 (_2, not_3_out, b, not_1_out);
  and and_4 (_3, not_3_out, b, c);
  and and_5 (_4, a, not_2_out, not_1_out);
  and and_6 (_5, a, not_2_out, c);
  and and_7 (_6, a, b, not_1_out);
  and and_8 (_7, a, b, c);

  // Notes on the sheet:
  //   a: pull=down
  //   b: pull=down
  //   c: pull=down
endmodule

module CPU_STEPPER (
  input  reset,
  input  clk,
  output step_1,
  output step_2,
  output step_3,
  output step_4,
  output step_5,
  output step_6,
  output step_7
);

  wire cpu_mem_1_1_out_3, cpu_mem_1_2_out_3, cpu_mem_1_3_out_3, cpu_mem_1_4_out_3, cpu_mem_1_5_out_3,
       cpu_mem_1_6_out_3, cpu_mem_1_7_out_3, cpu_mem_1_8_out_3, cpu_mem_1_9_out_3, cpu_mem_1_10_out_3,
       cpu_mem_1_11_out_3, not_1_out, not_2_out, not_3_out, not_4_out, not_5_out, not_6_out, not_7_out,
       not_8_out, or_1_out, or_2_out;

  not not_1 (not_1_out, clk);
  not not_2 (not_2_out, reset);
  or or_1 (or_1_out, reset, clk);
  or or_2 (or_2_out, reset, not_1_out);
  or or_3 (step_1, reset, not_3_out);
  CPU_MEM_1 cpu_mem_1_1 (.in_1(not_2_out), .out_3(cpu_mem_1_1_out_3), .in_2(or_1_out));
  not not_3 (not_3_out, cpu_mem_1_2_out_3);
  CPU_MEM_1 cpu_mem_1_2 (.in_1(cpu_mem_1_1_out_3), .out_3(cpu_mem_1_2_out_3), .in_2(or_2_out));
  and and_1 (step_2, cpu_mem_1_2_out_3, not_4_out);
  not not_4 (not_4_out, cpu_mem_1_4_out_3);
  CPU_MEM_1 cpu_mem_1_3 (.in_1(cpu_mem_1_2_out_3), .out_3(cpu_mem_1_3_out_3), .in_2(or_1_out));
  CPU_MEM_1 cpu_mem_1_4 (.in_1(cpu_mem_1_3_out_3), .out_3(cpu_mem_1_4_out_3), .in_2(or_2_out));
  and and_2 (step_3, cpu_mem_1_4_out_3, not_5_out);
  CPU_MEM_1 cpu_mem_1_5 (.in_1(cpu_mem_1_4_out_3), .out_3(cpu_mem_1_5_out_3), .in_2(or_1_out));
  not not_5 (not_5_out, cpu_mem_1_6_out_3);
  CPU_MEM_1 cpu_mem_1_6 (.in_1(cpu_mem_1_5_out_3), .out_3(cpu_mem_1_6_out_3), .in_2(or_2_out));
  and and_3 (step_4, cpu_mem_1_6_out_3, not_6_out);
  not not_6 (not_6_out, cpu_mem_1_8_out_3);
  CPU_MEM_1 cpu_mem_1_7 (.in_1(cpu_mem_1_6_out_3), .out_3(cpu_mem_1_7_out_3), .in_2(or_1_out));
  and and_4 (step_5, cpu_mem_1_8_out_3, not_7_out);
  CPU_MEM_1 cpu_mem_1_8 (.in_1(cpu_mem_1_7_out_3), .out_3(cpu_mem_1_8_out_3), .in_2(or_2_out));
  CPU_MEM_1 cpu_mem_1_9 (.in_1(cpu_mem_1_8_out_3), .out_3(cpu_mem_1_9_out_3), .in_2(or_1_out));
  not not_7 (not_7_out, cpu_mem_1_10_out_3);
  CPU_MEM_1 cpu_mem_1_10 (.in_1(cpu_mem_1_9_out_3), .out_3(cpu_mem_1_10_out_3), .in_2(or_2_out));
  and and_5 (step_6, cpu_mem_1_10_out_3, not_8_out);
  CPU_MEM_1 cpu_mem_1_11 (.in_1(cpu_mem_1_10_out_3), .out_3(cpu_mem_1_11_out_3), .in_2(or_1_out));
  not not_8 (not_8_out, step_7);
  CPU_MEM_1 cpu_mem_1_12 (.in_1(cpu_mem_1_11_out_3), .out_3(step_7), .in_2(or_2_out));

  // Notes on the sheet:
  //   reset: pull=down
endmodule

module CPU_DECODER_2X4 (
  input  a,
  input  b,
  output _0,
  output _1,
  output _2,
  output _3
);

  wire not_1_out, not_2_out;

  not not_1 (not_1_out, b);
  not not_2 (not_2_out, a);
  and and_1 (_0, not_2_out, not_1_out);
  and and_2 (_1, a, not_1_out);
  and and_3 (_2, b, not_2_out);
  and and_4 (_3, b, a);

  // Notes on the sheet:
  //   b: pull=down
  //   a: pull=down
endmodule

module CPU_DECODER_2x4_WEST (
  input  a,
  input  b,
  output _0,
  output _1,
  output _2,
  output _3
);

  wire not_1_out, not_2_out;

  not not_1 (not_1_out, b);
  not not_2 (not_2_out, a);
  and and_1 (_0, not_2_out, not_1_out);
  and and_2 (_1, a, not_1_out);
  and and_3 (_2, b, not_2_out);
  and and_4 (_3, b, a);

  // Notes on the sheet:
  //   b: pull=down
  //   a: pull=down
endmodule
